// Logisim project CRC.circ as structural Verilog
module _4bit_mod (
  input  [3:0] dividend,
  input  [3:0] divisor,
  output [2:0] remainder,
  output quotient
);

  wire [3:0] xor_1_out;
  wire [3:3] multiplexer_1_out;

  BitSelector #(.width(4)) bitselector_1 (.in(dividend), .out(quotient), .sel(2'b11));
  Multiplexer #(.width(4)) multiplexer_1 (
    .in0(dividend), .in1(xor_1_out), .out({multiplexer_1_out[3], remainder}), .sel(quotient));  // open: en
  assign xor_1_out = dividend ^ divisor;  // XOR_Gate xor_1, 4 bits wide
endmodule

module CRC (
  input  [7:0] A,
  input  [3:0] B,
  output [10:0] res
);

  wire bit0, bit1, bit2, bit3, bit4, bit5, bit6;
  wire [2:0] n4bit_mod_1_remainder, n4bit_mod_2_remainder, n4bit_mod_3_remainder, n4bit_mod_4_remainder,
       n4bit_mod_5_remainder, n4bit_mod_6_remainder;
  wire [3:1] n4bit_mod_7_remainder;
  wire [10:0] bit_extender_1_out;
  wire [10:7] shifter_1_out;

  assign bit_extender_1_out = {{3{1'b0}}, A};  // Bit_Extender bit_extender_1
  Shifter #(.width(11)) shifter_1 (
    .in(bit_extender_1_out), .\dist (4'b0011), .out({shifter_1_out, bit6, bit5, bit4, bit3, bit2, bit1, bit0}));
  _4bit_mod u_4bit_mod_1 (.dividend(shifter_1_out), .divisor(B), .remainder(n4bit_mod_1_remainder));  // open: quotient
  _4bit_mod u_4bit_mod_2 (
    .dividend({n4bit_mod_7_remainder, bit3}), .divisor(B), .remainder(n4bit_mod_2_remainder));  // open: quotient
  // Probe on {n4bit_mod_1_remainder, bit6}
  _4bit_mod u_4bit_mod_3 (
    .dividend({n4bit_mod_1_remainder, bit6}), .divisor(B), .remainder(n4bit_mod_3_remainder));  // open: quotient
  _4bit_mod u_4bit_mod_4 (
    .dividend({n4bit_mod_2_remainder, bit2}), .divisor(B), .remainder(n4bit_mod_4_remainder));  // open: quotient
  _4bit_mod u_4bit_mod_5 (
    .dividend({n4bit_mod_3_remainder, bit5}), .divisor(B), .remainder(n4bit_mod_5_remainder));  // open: quotient
  _4bit_mod u_4bit_mod_6 (
    .dividend({n4bit_mod_4_remainder, bit1}), .divisor(B), .remainder(n4bit_mod_6_remainder));  // open: quotient
  _4bit_mod u_4bit_mod_7 (
    .dividend({n4bit_mod_5_remainder, bit4}), .divisor(B), .remainder(n4bit_mod_7_remainder));  // open: quotient
  _4bit_mod u_4bit_mod_8 (
    .dividend({n4bit_mod_6_remainder, bit0}), .divisor(B), .remainder(res[2:0]));  // open: quotient

  assign res[10:3] = A;

  // Other names for the same wires on the sheet: divisor[3:0] = B; remainder[2:0] = res[2:0]
endmodule
