// Logisim project GRF.circ as structural Verilog: 2 circuits, main circuit grf
module grf (
  input  clk,
  input  WE,
  input  reset,
  input  [31:0] WD,
  input  [4:0] A1,
  input  [4:0] A2,
  input  [4:0] A3,
  output [31:0] RD1,
  output [31:0] RD2
);

  wire [31:0] _1_in, _1_out, _2_in, _2_out, _3_in, _3_out, _4_in, _4_out, _5_in, _5_out, _6_in, _6_out,
       _7_in, _7_out, _8_in, _8_out, _9_in, _9_out, _10_in, _10_out, _11_in, _11_out, _12_in, _12_out,
       _13_in, _13_out, _14_in, _14_out, _15_in, _15_out, _16_in, _16_out, _17_in, _17_out, _18_in, _18_out,
       _19_in, _19_out, _20_in, _20_out, _21_in, _21_out, _22_in, _22_out, _23_in, _23_out, _24_in, _24_out,
       _25_in, _25_out, _26_in, _26_out, _27_in, _27_out, _28_in, _28_out, _29_in, _29_out, _30_in, _30_out,
       _31_in, _31_out;

  Multiplexer #(.select(5), .width(32)) multiplexer_1 (
    .in0({32{1'b0}}), .in1(_1_out), .in2(_2_out), .in3(_3_out), .in4(_4_out), .in5(_5_out), .in6(_6_out),
    .in7(_7_out), .in8(_8_out), .in9(_9_out), .in10(_10_out), .in11(_11_out), .in12(_12_out), .in13(_13_out),
    .in14(_14_out), .in15(_15_out), .in16(_16_out), .in17(_17_out), .in18(_18_out), .in19(_19_out),
    .in20(_20_out), .in21(_21_out), .in22(_22_out), .in23(_23_out), .in24(_24_out), .in25(_25_out),
    .in26(_26_out), .in27(_27_out), .in28(_28_out), .in29(_29_out), .in30(_30_out), .in31(_31_out),
    .out(RD1), .sel(A1));  // open: en
  Register #(.width(32)) register_1 (.D({32{1'b0}}), .en(WE), .clk(clk), .clr(reset));  // open: Q
  Register #(.width(32)) register_2 (.D(_8_in), .en(WE), .Q(_8_out), .clk(clk), .clr(reset));
  Register #(.width(32)) register_3 (.D(_16_in), .en(WE), .Q(_16_out), .clk(clk), .clr(reset));
  Register #(.width(32)) register_4 (.D(_24_in), .en(WE), .Q(_24_out), .clk(clk), .clr(reset));
  Register #(.width(32)) register_5 (.D(_1_in), .en(WE), .Q(_1_out), .clk(clk), .clr(reset));
  Register #(.width(32)) register_6 (.D(_9_in), .en(WE), .Q(_9_out), .clk(clk), .clr(reset));
  Register #(.width(32)) register_7 (.D(_17_in), .en(WE), .Q(_17_out), .clk(clk), .clr(reset));
  Register #(.width(32)) register_8 (.D(_25_in), .en(WE), .Q(_25_out), .clk(clk), .clr(reset));
  Multiplexer #(.select(5), .width(32)) multiplexer_2 (
    .in0({32{1'b0}}), .in1(_1_out), .in2(_2_out), .in3(_3_out), .in4(_4_out), .in5(_5_out), .in6(_6_out),
    .in7(_7_out), .in8(_8_out), .in9(_9_out), .in10(_10_out), .in11(_11_out), .in12(_12_out), .in13(_13_out),
    .in14(_14_out), .in15(_15_out), .in16(_16_out), .in17(_17_out), .in18(_18_out), .in19(_19_out),
    .in20(_20_out), .in21(_21_out), .in22(_22_out), .in23(_23_out), .in24(_24_out), .in25(_25_out),
    .in26(_26_out), .in27(_27_out), .in28(_28_out), .in29(_29_out), .in30(_30_out), .in31(_31_out),
    .out(RD2), .sel(A2));  // open: en
  Register #(.width(32)) register_9 (.D(_2_in), .en(WE), .Q(_2_out), .clk(clk), .clr(reset));
  Register #(.width(32)) register_10 (.D(_10_in), .en(WE), .Q(_10_out), .clk(clk), .clr(reset));
  Register #(.width(32)) register_11 (.D(_18_in), .en(WE), .Q(_18_out), .clk(clk), .clr(reset));
  Register #(.width(32)) register_12 (.D(_26_in), .en(WE), .Q(_26_out), .clk(clk), .clr(reset));
  Register #(.width(32)) register_13 (.D(_3_in), .en(WE), .Q(_3_out), .clk(clk), .clr(reset));
  Register #(.width(32)) register_14 (.D(_11_in), .en(WE), .Q(_11_out), .clk(clk), .clr(reset));
  Register #(.width(32)) register_15 (.D(_19_in), .en(WE), .Q(_19_out), .clk(clk), .clr(reset));
  Register #(.width(32)) register_16 (.D(_27_in), .en(WE), .Q(_27_out), .clk(clk), .clr(reset));
  Demultiplexer #(.select(5), .width(32), .tristate("true"), .disabled(0)) demultiplexer_1 (
    .out1(_1_in), .out2(_2_in), .out3(_3_in), .out4(_4_in), .out5(_5_in), .out6(_6_in), .out7(_7_in),
    .out8(_8_in), .out9(_9_in), .out10(_10_in), .out11(_11_in), .out12(_12_in), .out13(_13_in),
    .out14(_14_in), .out15(_15_in), .out16(_16_in), .out17(_17_in), .out18(_18_in), .out19(_19_in),
    .out20(_20_in), .out21(_21_in), .out22(_22_in), .out23(_23_in), .out24(_24_in), .out25(_25_in),
    .out26(_26_in), .out27(_27_in), .out28(_28_in), .out29(_29_in), .out30(_30_in), .out31(_31_in), .in(WD),
    .sel(A3));  // open: out0, en
  Register #(.width(32)) register_17 (.D(_4_in), .en(WE), .Q(_4_out), .clk(clk), .clr(reset));
  Register #(.width(32)) register_18 (.D(_12_in), .en(WE), .Q(_12_out), .clk(clk), .clr(reset));
  Register #(.width(32)) register_19 (.D(_20_in), .en(WE), .Q(_20_out), .clk(clk), .clr(reset));
  Register #(.width(32)) register_20 (.D(_28_in), .en(WE), .Q(_28_out), .clk(clk), .clr(reset));
  Register #(.width(32)) register_21 (.D(_5_in), .en(WE), .Q(_5_out), .clk(clk), .clr(reset));
  Register #(.width(32)) register_22 (.D(_13_in), .en(WE), .Q(_13_out), .clk(clk), .clr(reset));
  Register #(.width(32)) register_23 (.D(_21_in), .en(WE), .Q(_21_out), .clk(clk), .clr(reset));
  Register #(.width(32)) register_24 (.D(_29_in), .en(WE), .Q(_29_out), .clk(clk), .clr(reset));
  Register #(.width(32)) register_25 (.D(_6_in), .en(WE), .Q(_6_out), .clk(clk), .clr(reset));
  Register #(.width(32)) register_26 (.D(_14_in), .en(WE), .Q(_14_out), .clk(clk), .clr(reset));
  Register #(.width(32)) register_27 (.D(_22_in), .en(WE), .Q(_22_out), .clk(clk), .clr(reset));
  Register #(.width(32)) register_28 (.D(_30_in), .en(WE), .Q(_30_out), .clk(clk), .clr(reset));
  Register #(.width(32)) register_29 (.D(_7_in), .en(WE), .Q(_7_out), .clk(clk), .clr(reset));
  Register #(.width(32)) register_30 (.D(_15_in), .en(WE), .Q(_15_out), .clk(clk), .clr(reset));
  Register #(.width(32)) register_31 (.D(_23_in), .en(WE), .Q(_23_out), .clk(clk), .clr(reset));
  Register #(.width(32)) register_32 (.D(_31_in), .en(WE), .Q(_31_out), .clk(clk), .clr(reset));
endmodule

module test (
  input  in_1,
  input  in_2,
  input  [4:0] in_3,
  input  [4:0] in_4,
  input  [4:0] in_5,
  input  [31:0] in_6,
  output [31:0] out_7,
  output [31:0] out_8
);

  wire clock_1_out;

  Clock clock_1 (.out(clock_1_out));
  grf grf_1 (
    .clk(clock_1_out), .WE(in_2), .reset(in_1), .WD(in_6), .A1(in_3), .A2(in_4), .A3(in_5), .RD1(out_7),
    .RD2(out_8));
endmodule
