// Logisim project dir.circ as structural Verilog: 3 circuits, main circuit main
module main (
  input  [1:0] Dir,
  input  clk,
  input  reset,
  output [3:0] out_4
);

  wire [2:0] register_1_q, statetransfer_1_nextstate;

  StateTransfer statetransfer_1 (.State(register_1_q), .Dir(Dir), .NextState(statetransfer_1_nextstate));
  Register #(.width(3)) register_1 (
    .D(statetransfer_1_nextstate), .Q(register_1_q), .clk(clk), .clr(reset));  // open: en
  Output output_1 (.State(register_1_q), .Dir(Dir), .out_3(out_4));
endmodule

module StateTransfer (
  input  [2:0] State,
  input  [1:0] Dir,
  output [2:0] NextState
);

  wire and_1_out, and_2_out, and_3_out, and_4_out, and_5_out, and_6_out, and_7_out, and_8_out, and_9_out,
       and_10_out, and_11_out, and_12_out, and_13_out, and_14_out, and_15_out, and_16_out, and_17_out,
       and_18_out, and_19_out, and_20_out, not_1_out, not_2_out, not_3_out, not_4_out, not_5_out, not_6_out,
       not_7_out, not_8_out, not_9_out, not_10_out, not_11_out, not_12_out, not_13_out, not_14_out,
       not_15_out, not_16_out, not_17_out, not_18_out, not_19_out, not_20_out, not_21_out, not_22_out,
       not_23_out, not_24_out, not_25_out, not_26_out, not_27_out, not_28_out, not_29_out, not_30_out,
       not_31_out, not_32_out, not_33_out, not_34_out, not_35_out, not_36_out;

  not not_1 (not_1_out, State[1]);
  not not_2 (not_2_out, State[0]);
  not not_3 (not_3_out, Dir[0]);
  not not_4 (not_4_out, Dir[0]);
  not not_5 (not_5_out, Dir[1]);
  not not_6 (not_6_out, State[1]);
  not not_7 (not_7_out, State[0]);
  not not_8 (not_8_out, State[2]);
  not not_9 (not_9_out, State[0]);
  not not_10 (not_10_out, Dir[0]);
  not not_11 (not_11_out, State[2]);
  not not_12 (not_12_out, Dir[1]);
  not not_13 (not_13_out, State[2]);
  not not_14 (not_14_out, Dir[1]);
  not not_15 (not_15_out, State[0]);
  not not_16 (not_16_out, Dir[1]);
  not not_17 (not_17_out, Dir[0]);
  not not_18 (not_18_out, Dir[0]);
  not not_19 (not_19_out, State[2]);
  not not_20 (not_20_out, State[1]);
  not not_21 (not_21_out, State[0]);
  not not_22 (not_22_out, Dir[1]);
  not not_23 (not_23_out, State[2]);
  not not_24 (not_24_out, State[1]);
  not not_25 (not_25_out, Dir[0]);
  not not_26 (not_26_out, State[1]);
  not not_27 (not_27_out, State[2]);
  not not_28 (not_28_out, State[0]);
  not not_29 (not_29_out, Dir[0]);
  not not_30 (not_30_out, Dir[1]);
  not not_31 (not_31_out, State[1]);
  not not_32 (not_32_out, State[0]);
  not not_33 (not_33_out, Dir[1]);
  not not_34 (not_34_out, Dir[0]);
  not not_35 (not_35_out, State[1]);
  not not_36 (not_36_out, State[0]);
  and and_1 (and_1_out, not_1_out, not_2_out, Dir[1], not_3_out);
  and and_2 (and_2_out, State[1], State[0], Dir[1], not_4_out);
  and and_3 (and_3_out, State[2], not_5_out);
  and and_4 (and_4_out, State[2], not_6_out, State[0]);
  and and_5 (and_5_out, State[2], State[1], not_7_out);
  and and_6 (and_6_out, not_8_out, not_9_out, Dir[1], not_10_out);
  and and_7 (and_7_out, not_11_out, State[0], not_12_out, Dir[0]);
  and and_8 (and_8_out, not_13_out, State[1], Dir[0]);
  and and_9 (and_9_out, State[1], State[0], not_14_out);
  and and_10 (and_10_out, State[2], not_15_out, Dir[1], Dir[0]);
  and and_11 (and_11_out, State[2], State[0], not_16_out, not_17_out);
  and and_12 (and_12_out, State[2], State[1], not_18_out);
  and and_13 (and_13_out, not_19_out, not_20_out, not_21_out, not_22_out, Dir[0]);
  and and_14 (and_14_out, not_23_out, not_24_out, Dir[1], not_25_out);
  and and_15 (and_15_out, not_26_out, State[0], Dir[1]);
  and and_16 (and_16_out, not_27_out, State[1], not_28_out, not_29_out);
  and and_17 (and_17_out, State[1], State[0], not_30_out);
  and and_18 (and_18_out, State[2], not_31_out, not_32_out, not_33_out, not_34_out);
  and and_19 (and_19_out, State[2], not_35_out, Dir[1], Dir[0]);
  and and_20 (and_20_out, State[2], State[1], not_36_out, Dir[0]);
  or or_1 (NextState[2], and_1_out, and_2_out, and_3_out, and_4_out, and_5_out);
  or or_2 (NextState[1], and_6_out, and_7_out, and_8_out, and_9_out, and_10_out, and_11_out, and_12_out);
  or or_3 (NextState[0], and_13_out, and_14_out, and_15_out, and_16_out, and_17_out, and_18_out, and_19_out, and_20_out);
endmodule

module Output (
  input  [2:0] State,
  input  [1:0] Dir,
  output [3:0] out_3
);

  wire and_1_out, and_2_out, and_3_out, and_4_out, and_5_out, and_6_out, and_7_out, and_8_out, and_9_out,
       and_10_out, and_11_out, and_12_out, and_13_out, and_14_out, and_15_out, and_16_out, and_17_out,
       and_18_out, and_19_out, and_20_out, not_1_out, not_2_out, not_3_out, not_4_out, not_5_out, not_6_out,
       not_7_out, not_8_out, not_9_out, not_10_out, not_11_out, not_12_out, not_13_out, not_14_out,
       not_15_out, not_16_out, not_17_out, not_18_out, not_19_out, not_20_out, not_21_out, not_22_out,
       not_23_out, not_24_out, not_25_out, not_26_out, not_27_out, not_28_out, not_29_out, not_30_out,
       not_31_out, not_32_out, not_33_out, not_34_out, not_35_out, not_36_out;
  wire [2:0] or_3_out;
  wire [3:0] bit_extender_1_out;

  not not_1 (not_1_out, State[1]);
  not not_2 (not_2_out, State[0]);
  not not_3 (not_3_out, Dir[0]);
  not not_4 (not_4_out, Dir[0]);
  not not_5 (not_5_out, Dir[1]);
  not not_6 (not_6_out, State[1]);
  not not_7 (not_7_out, State[0]);
  not not_8 (not_8_out, State[2]);
  not not_9 (not_9_out, State[0]);
  not not_10 (not_10_out, Dir[0]);
  not not_11 (not_11_out, State[2]);
  not not_12 (not_12_out, Dir[1]);
  not not_13 (not_13_out, State[2]);
  not not_14 (not_14_out, Dir[1]);
  not not_15 (not_15_out, State[0]);
  not not_16 (not_16_out, Dir[1]);
  not not_17 (not_17_out, Dir[0]);
  not not_18 (not_18_out, Dir[0]);
  not not_19 (not_19_out, State[2]);
  not not_20 (not_20_out, State[1]);
  not not_21 (not_21_out, State[0]);
  not not_22 (not_22_out, Dir[1]);
  not not_23 (not_23_out, State[2]);
  not not_24 (not_24_out, State[1]);
  not not_25 (not_25_out, Dir[0]);
  not not_26 (not_26_out, State[1]);
  not not_27 (not_27_out, State[2]);
  not not_28 (not_28_out, State[0]);
  not not_29 (not_29_out, Dir[0]);
  not not_30 (not_30_out, Dir[1]);
  not not_31 (not_31_out, State[1]);
  not not_32 (not_32_out, State[0]);
  not not_33 (not_33_out, Dir[1]);
  not not_34 (not_34_out, Dir[0]);
  not not_35 (not_35_out, State[1]);
  not not_36 (not_36_out, State[0]);
  and and_1 (and_1_out, not_1_out, not_2_out, Dir[1], not_3_out);
  and and_2 (and_2_out, State[1], State[0], Dir[1], not_4_out);
  and and_3 (and_3_out, State[2], not_5_out);
  and and_4 (and_4_out, State[2], not_6_out, State[0]);
  and and_5 (and_5_out, State[2], State[1], not_7_out);
  and and_6 (and_6_out, not_8_out, not_9_out, Dir[1], not_10_out);
  and and_7 (and_7_out, not_11_out, State[0], not_12_out, Dir[0]);
  and and_8 (and_8_out, not_13_out, State[1], Dir[0]);
  and and_9 (and_9_out, State[1], State[0], not_14_out);
  and and_10 (and_10_out, State[2], not_15_out, Dir[1], Dir[0]);
  and and_11 (and_11_out, State[2], State[0], not_16_out, not_17_out);
  and and_12 (and_12_out, State[2], State[1], not_18_out);
  and and_13 (and_13_out, not_19_out, not_20_out, not_21_out, not_22_out, Dir[0]);
  and and_14 (and_14_out, not_23_out, not_24_out, Dir[1], not_25_out);
  and and_15 (and_15_out, not_26_out, State[0], Dir[1]);
  and and_16 (and_16_out, not_27_out, State[1], not_28_out, not_29_out);
  and and_17 (and_17_out, State[1], State[0], not_30_out);
  and and_18 (and_18_out, State[2], not_31_out, not_32_out, not_33_out, not_34_out);
  and and_19 (and_19_out, State[2], not_35_out, Dir[1], Dir[0]);
  and and_20 (and_20_out, State[2], State[1], not_36_out, Dir[0]);
  or or_1 (or_3_out[2], and_1_out, and_2_out, and_3_out, and_4_out, and_5_out);
  or or_2 (or_3_out[1], and_6_out, and_7_out, and_8_out, and_9_out, and_10_out, and_11_out, and_12_out);
  or or_3 (or_3_out[0], and_13_out, and_14_out, and_15_out, and_16_out, and_17_out, and_18_out, and_19_out, and_20_out);
  assign bit_extender_1_out = {{1{1'b0}}, or_3_out};  // Bit_Extender bit_extender_1
  Adder #(.width(4)) adder_1 (.a(bit_extender_1_out), .b(4'b0001), .out(out_3));  // open: cin, cout
endmodule
