// Logisim project fsm.circ as structural Verilog
module StateTransfer (
  input  [2:0] State,
  input  [1:0] Input,
  output [2:0] nextState
);

  wire and_2_out, and_3_out, and_4_out, and_5_out, and_6_out, and_7_out, and_8_out, and_9_out, not_1_out,
       not_2_out, not_3_out, not_4_out, not_5_out, not_6_out, not_7_out, not_8_out, not_9_out, not_10_out,
       not_11_out, not_12_out, not_13_out, not_14_out, not_15_out, not_16_out, not_17_out;

  not not_1 (not_1_out, Input[0]);
  not not_2 (not_2_out, State[1]);
  not not_3 (not_3_out, Input[1]);
  not not_4 (not_4_out, State[1]);
  not not_5 (not_5_out, Input[0]);
  not not_6 (not_6_out, State[0]);
  not not_7 (not_7_out, Input[1]);
  not not_8 (not_8_out, State[0]);
  not not_9 (not_9_out, Input[0]);
  not not_10 (not_10_out, State[1]);
  not not_11 (not_11_out, State[0]);
  not not_12 (not_12_out, Input[1]);
  not not_13 (not_13_out, Input[1]);
  and and_1 (nextState[2], State[1], State[0], not_1_out);
  and and_2 (and_2_out, not_2_out, State[0], not_3_out);
  and and_3 (and_3_out, not_4_out, State[0], not_5_out);
  and and_4 (and_4_out, State[1], not_6_out, not_7_out);
  and and_5 (and_5_out, State[1], not_8_out, not_9_out);
  and and_6 (and_6_out, not_10_out, not_11_out, not_12_out, Input[0]);
  not not_14 (not_14_out, State[1]);
  and and_7 (and_7_out, not_14_out, State[0], not_15_out);
  not not_15 (not_15_out, Input[0]);
  not not_16 (not_16_out, State[0]);
  and and_8 (and_8_out, State[1], not_16_out, not_17_out);
  not not_17 (not_17_out, Input[0]);
  and and_9 (and_9_out, State[1], State[0], not_13_out, Input[0]);
  or or_1 (nextState[1], and_2_out, and_3_out, and_4_out, and_5_out);
  or or_2 (nextState[0], and_6_out, and_7_out, and_8_out, and_9_out);
endmodule

module Output (
  input  [2:0] State,
  input  [1:0] Input,
  output Output
);

  wire not_1_out;

  not not_1 (not_1_out, Input[0]);
  and and_1 (Output, State[1], State[0], not_1_out);
endmodule

module fsm (
  input  [1:0] \input ,
  input  Clr,
  output out_3
);

  wire clock_1_out;
  wire [2:0] multiplexer_1_out, register_1_q, statetransfer_1_nextstate;

  StateTransfer statetransfer_1 (.State(register_1_q), .Input(\input ), .nextState(statetransfer_1_nextstate));
  Multiplexer #(.width(3)) multiplexer_1 (
    .in0(statetransfer_1_nextstate), .in1(3'b000), .out(multiplexer_1_out), .sel(Clr));  // open: en
  Register #(.width(3)) register_1 (.D(multiplexer_1_out), .Q(register_1_q), .clk(clock_1_out));  // open: en, clr
  Clock clock_1 (.out(clock_1_out));
  Output output_1 (.State(register_1_q), .Input(\input ), .Output(out_3));
endmodule
