// Logisim project ftoi.circ as structural Verilog
module ftoi (
  input  [15:0] float,
  output [31:0] \int 
);

  wire bitselector_1_out, Denormalized, InfinityOrNaN, neg, or_1_out;
  wire [4:0] bitfinder_1_index, move, negator_1_out, subtractor_1_out;
  wire [10:0] bit_extender_1_out;
  wire [31:0] bit_extender_2_out, multiplexer_1_out, multiplexer_2_out, negator_2_out, shifter_1_out,
       shifter_2_out;

  assign bit_extender_1_out = {{1{1'b1}}, float[9:0]};  // Bit_Extender bit_extender_1
  // Probe on bit_extender_2_out
  assign bit_extender_2_out = {{21{1'b0}}, bit_extender_1_out};  // Bit_Extender bit_extender_2
  BitFinder #(.width(32), .\type ("high1")) bitfinder_1 (
    .in(bit_extender_2_out), .index(bitfinder_1_index));  // open: found
  Subtractor #(.width(5)) subtractor_1 (.a(bitfinder_1_index), .b(move), .out(subtractor_1_out));  // open: bin, bout
  BitSelector #(.width(5)) bitselector_1 (.in(subtractor_1_out), .out(bitselector_1_out), .sel(3'b100));
  Negator #(.width(5)) negator_1 (.in(subtractor_1_out), .out(negator_1_out));
  Shifter #(.width(32), .shift("lr")) shifter_1 (
    .in(bit_extender_2_out), .\dist (subtractor_1_out), .out(shifter_1_out));
  Shifter #(.width(32)) shifter_2 (.in(bit_extender_2_out), .\dist (negator_1_out), .out(shifter_2_out));
  Multiplexer #(.width(32)) multiplexer_1 (
    .in0(shifter_1_out), .in1(shifter_2_out), .out(multiplexer_1_out), .sel(bitselector_1_out));  // open: en
  Comparator #(.width(5)) comparator_1 (.a(float[14:10]), .b({5{1'b0}}), .eq(Denormalized));  // open: gt, lt
  Comparator #(.width(5)) comparator_2 (.a(float[14:10]), .b({5{1'b1}}), .eq(InfinityOrNaN));  // open: gt, lt
  Subtractor #(.width(5)) subtractor_2 (.a(float[14:10]), .b(5'b01111), .out(move));  // open: bin, bout
  // Probe on move
  Negator #(.width(32)) negator_2 (.in(multiplexer_1_out), .out(negator_2_out));
  Multiplexer #(.width(32)) multiplexer_2 (
    .in0(multiplexer_1_out), .in1(negator_2_out), .out(multiplexer_2_out), .sel(float[15]));  // open: en
  BitSelector #(.width(5)) bitselector_2 (.in(move), .out(neg), .sel(3'b100));
  Multiplexer #(.width(32)) multiplexer_3 (
    .in0(multiplexer_2_out), .in1({32{1'b0}}), .out(\int ), .sel(or_1_out));  // open: en
  or or_1 (or_1_out, InfinityOrNaN, Denormalized, neg);

  // Other names for the same wires on the sheet: fraction[9:0] = float[9:0]; exponent[4:0] = float[14:10];
  //   sign = float[15]
endmodule
