// Logisim project min.circ as structural Verilog: 1 circuit, main circuit main
module main (
  input  [7:0] n1,
  input  [7:0] n2,
  input  [7:0] n3,
  input  [7:0] n4,
  input  [7:0] n5,
  output [7:0] min
);

  wire comparator_1_eq, comparator_2_eq, comparator_3_eq, comparator_4_eq, comparator_5_eq, comparator_6_eq,
       comparator_7_eq, comparator_8_eq, comparator_9_eq, comparator_10_eq, comparator_11_eq,
       comparator_12_eq, comparator_13_eq, comparator_14_eq, comparator_15_eq, comparator_16_eq,
       comparator_17_eq, comparator_18_eq, comparator_19_eq, comparator_20_eq, comparator_21_eq,
       comparator_22_eq, comparator_23_eq, comparator_24_eq, comparator_25_eq, or_1_out, or_2_out, or_3_out,
       or_4_out, or_5_out, res1, res2, res3, res4, res5;
  wire [7:0] multiplexer_1_out, multiplexer_2_out, multiplexer_3_out, multiplexer_4_out;

  Comparator comparator_1 (.a(8'h3), .b(n1), .eq(comparator_1_eq));  // open: gt, lt
  Comparator comparator_2 (.a(8'h3), .b(n2), .eq(comparator_2_eq));  // open: gt, lt
  Comparator comparator_3 (.a(8'h3), .b(n3), .eq(comparator_3_eq));  // open: gt, lt
  Comparator comparator_4 (.a(8'h3), .b(n4), .eq(comparator_4_eq));  // open: gt, lt
  Comparator comparator_5 (.a(8'h3), .b(n5), .eq(comparator_5_eq));  // open: gt, lt
  Multiplexer #(.width(8)) multiplexer_1 (.in0(8'h6), .in1(8'h5), .out(multiplexer_1_out), .sel(res5));  // open: en
  Comparator comparator_6 (.a(8'h1), .b(n1), .eq(comparator_6_eq));  // open: gt, lt
  Comparator comparator_7 (.a(8'h1), .b(n2), .eq(comparator_7_eq));  // open: gt, lt
  Comparator comparator_8 (.a(8'h1), .b(n3), .eq(comparator_8_eq));  // open: gt, lt
  Comparator comparator_9 (.a(8'h1), .b(n4), .eq(comparator_9_eq));  // open: gt, lt
  Comparator comparator_10 (.a(8'h1), .b(n5), .eq(comparator_10_eq));  // open: gt, lt
  or or_1 (or_1_out, comparator_1_eq, comparator_2_eq, comparator_3_eq, comparator_4_eq, comparator_5_eq);
  not not_1 (res3, or_1_out);
  Multiplexer #(.width(8)) multiplexer_2 (
    .in0(multiplexer_1_out), .in1(8'h4), .out(multiplexer_2_out), .sel(res4));  // open: en
  Multiplexer #(.width(8)) multiplexer_3 (
    .in0(multiplexer_2_out), .in1(8'h3), .out(multiplexer_3_out), .sel(res3));  // open: en
  not not_2 (res1, or_2_out);
  or or_2 (or_2_out, comparator_6_eq, comparator_7_eq, comparator_8_eq, comparator_9_eq, comparator_10_eq);
  Multiplexer #(.width(8)) multiplexer_4 (
    .in0(multiplexer_3_out), .in1(8'h2), .out(multiplexer_4_out), .sel(res2));  // open: en
  Comparator comparator_11 (.a(8'h4), .b(n1), .eq(comparator_11_eq));  // open: gt, lt
  Comparator comparator_12 (.a(8'h4), .b(n2), .eq(comparator_12_eq));  // open: gt, lt
  Comparator comparator_13 (.a(8'h4), .b(n3), .eq(comparator_13_eq));  // open: gt, lt
  Comparator comparator_14 (.a(8'h4), .b(n4), .eq(comparator_14_eq));  // open: gt, lt
  Comparator comparator_15 (.a(8'h4), .b(n5), .eq(comparator_15_eq));  // open: gt, lt
  Multiplexer #(.width(8)) multiplexer_5 (.in0(multiplexer_4_out), .in1(8'h1), .out(min), .sel(res1));  // open: en
  or or_3 (or_3_out, comparator_11_eq, comparator_12_eq, comparator_13_eq, comparator_14_eq, comparator_15_eq);
  not not_3 (res4, or_3_out);
  Comparator comparator_16 (.a(8'h2), .b(n1), .eq(comparator_16_eq));  // open: gt, lt
  Comparator comparator_17 (.a(8'h2), .b(n2), .eq(comparator_17_eq));  // open: gt, lt
  Comparator comparator_18 (.a(8'h2), .b(n3), .eq(comparator_18_eq));  // open: gt, lt
  Comparator comparator_19 (.a(8'h2), .b(n4), .eq(comparator_19_eq));  // open: gt, lt
  Comparator comparator_20 (.a(8'h2), .b(n5), .eq(comparator_20_eq));  // open: gt, lt
  or or_4 (or_4_out, comparator_16_eq, comparator_17_eq, comparator_18_eq, comparator_19_eq, comparator_20_eq);
  Comparator comparator_21 (.a(8'h5), .b(n1), .eq(comparator_21_eq));  // open: gt, lt
  Comparator comparator_22 (.a(8'h5), .b(n2), .eq(comparator_22_eq));  // open: gt, lt
  Comparator comparator_23 (.a(8'h5), .b(n3), .eq(comparator_23_eq));  // open: gt, lt
  Comparator comparator_24 (.a(8'h5), .b(n4), .eq(comparator_24_eq));  // open: gt, lt
  Comparator comparator_25 (.a(8'h5), .b(n5), .eq(comparator_25_eq));  // open: gt, lt
  not not_4 (res2, or_4_out);
  or or_5 (or_5_out, comparator_21_eq, comparator_22_eq, comparator_23_eq, comparator_24_eq, comparator_25_eq);
  not not_5 (res5, or_5_out);

  // Notes on the sheet:
  //   x
endmodule
