// Logisim project navigation.circ as structural Verilog
module StateTransfer (
  input  [2:0] State,
  input  [1:0] \input ,
  output [2:0] nextState
);

  wire and_1_out, and_2_out, and_3_out, and_4_out, and_5_out, and_6_out, and_7_out, and_8_out, and_9_out,
       and_10_out, and_11_out, not_1_out, not_2_out, not_3_out, not_4_out, not_5_out, not_6_out, not_7_out,
       not_8_out, not_9_out, not_10_out, not_11_out, not_12_out, not_13_out, not_14_out, not_15_out,
       not_16_out, not_17_out;

  not not_1 (not_1_out, State[0]);
  not not_2 (not_2_out, \input [1]);
  not not_3 (not_3_out, \input [0]);
  not not_4 (not_4_out, \input [1]);
  not not_5 (not_5_out, State[1]);
  not not_6 (not_6_out, \input [1]);
  not not_7 (not_7_out, \input [1]);
  not not_8 (not_8_out, \input [0]);
  not not_9 (not_9_out, State[0]);
  not not_10 (not_10_out, \input [1]);
  not not_11 (not_11_out, State[0]);
  not not_12 (not_12_out, \input [0]);
  not not_13 (not_13_out, State[2]);
  not not_14 (not_14_out, State[1]);
  not not_15 (not_15_out, \input [1]);
  not not_16 (not_16_out, \input [0]);
  not not_17 (not_17_out, \input [0]);
  and and_1 (and_1_out, State[1], not_1_out, not_2_out, not_3_out);
  and and_2 (and_2_out, State[1], State[0], not_4_out, \input [0]);
  and and_3 (and_3_out, not_5_out, State[0], not_6_out);
  and and_4 (and_4_out, State[0], not_7_out, not_8_out);
  and and_5 (and_5_out, State[1], not_9_out, not_10_out, \input [0]);
  and and_6 (and_6_out, State[1], not_11_out, \input [1], not_12_out);
  and and_7 (and_7_out, State[1], State[0], \input [1], \input [0]);
  and and_8 (and_8_out, not_13_out, not_14_out, not_15_out, not_16_out);
  and and_9 (and_9_out, State[0], \input [1], \input [0]);
  and and_10 (and_10_out, State[1], \input [1], \input [0]);
  and and_11 (and_11_out, State[1], State[0], not_17_out);
  or or_1 (nextState[2], and_1_out, and_2_out);
  or or_2 (nextState[1], and_3_out, and_4_out, and_5_out, and_6_out, and_7_out);
  or or_3 (nextState[0], and_8_out, and_9_out, and_10_out, and_11_out);
endmodule

module navigation (
  input  [1:0] \input ,
  input  clk,
  input  reset,
  output arrive,
  output hit
);

  wire comparator_1_eq;
  wire [2:0] register_1_q, statetransfer_1_nextstate;

  StateTransfer statetransfer_1 (.State(register_1_q), .\input (\input ), .nextState(statetransfer_1_nextstate));
  Register #(.width(3)) register_1 (
    .D(statetransfer_1_nextstate), .Q(register_1_q), .clk(clk), .clr(reset));  // open: en
  Register #(.width(1)) register_2 (.D(comparator_1_eq), .Q(hit), .clk(clk), .clr(reset));  // open: en
  Comparator #(.width(3), .mode("unsigned")) comparator_1 (
    .a(statetransfer_1_nextstate), .b(register_1_q), .eq(comparator_1_eq));  // open: gt, lt
  Comparator #(.width(3), .mode("unsigned")) comparator_2 (.a(register_1_q), .b(3'b100), .eq(arrive));  // open: gt, lt
endmodule
