// Logisim project CPU.circ as structural Verilog: 10 circuits, main circuit grf
module grf (
  input  clk,
  input  WE,
  input  reset,
  input  [31:0] WD,
  input  [4:0] A1,
  input  [4:0] A2,
  input  [4:0] A3,
  output [31:0] RD1,
  output [31:0] RD2
);

  wire [31:0] _1_in, _1_out, _2_in, _2_out, _3_in, _3_out, _4_in, _4_out, _5_in, _5_out, _6_in, _6_out,
       _7_in, _7_out, _8_in, _8_out, _9_in, _9_out, _10_in, _10_out, _11_in, _11_out, _12_in, _12_out,
       _13_in, _13_out, _14_in, _14_out, _15_in, _15_out, _16_in, _16_out, _17_in, _17_out, _18_in, _18_out,
       _19_in, _19_out, _20_in, _20_out, _21_in, _21_out, _22_in, _22_out, _23_in, _23_out, _24_in, _24_out,
       _25_in, _25_out, _26_in, _26_out, _27_in, _27_out, _28_in, _28_out, _29_in, _29_out, _30_in, _30_out,
       _31_in, _31_out;

  Multiplexer #(.select(5), .width(32)) multiplexer_1 (
    .in0({32{1'b0}}), .in1(_1_out), .in2(_2_out), .in3(_3_out), .in4(_4_out), .in5(_5_out), .in6(_6_out),
    .in7(_7_out), .in8(_8_out), .in9(_9_out), .in10(_10_out), .in11(_11_out), .in12(_12_out), .in13(_13_out),
    .in14(_14_out), .in15(_15_out), .in16(_16_out), .in17(_17_out), .in18(_18_out), .in19(_19_out),
    .in20(_20_out), .in21(_21_out), .in22(_22_out), .in23(_23_out), .in24(_24_out), .in25(_25_out),
    .in26(_26_out), .in27(_27_out), .in28(_28_out), .in29(_29_out), .in30(_30_out), .in31(_31_out),
    .out(RD1), .sel(A1));  // open: en
  Register #(.width(32)) register_1 (.D({32{1'b0}}), .en(WE), .clk(clk), .clr(reset));  // open: Q
  Register #(.width(32)) register_2 (.D(_8_in), .en(WE), .Q(_8_out), .clk(clk), .clr(reset));
  Register #(.width(32)) register_3 (.D(_16_in), .en(WE), .Q(_16_out), .clk(clk), .clr(reset));
  Register #(.width(32)) register_4 (.D(_24_in), .en(WE), .Q(_24_out), .clk(clk), .clr(reset));
  Register #(.width(32)) register_5 (.D(_1_in), .en(WE), .Q(_1_out), .clk(clk), .clr(reset));
  Register #(.width(32)) register_6 (.D(_9_in), .en(WE), .Q(_9_out), .clk(clk), .clr(reset));
  Register #(.width(32)) register_7 (.D(_17_in), .en(WE), .Q(_17_out), .clk(clk), .clr(reset));
  Register #(.width(32)) register_8 (.D(_25_in), .en(WE), .Q(_25_out), .clk(clk), .clr(reset));
  Multiplexer #(.select(5), .width(32)) multiplexer_2 (
    .in0({32{1'b0}}), .in1(_1_out), .in2(_2_out), .in3(_3_out), .in4(_4_out), .in5(_5_out), .in6(_6_out),
    .in7(_7_out), .in8(_8_out), .in9(_9_out), .in10(_10_out), .in11(_11_out), .in12(_12_out), .in13(_13_out),
    .in14(_14_out), .in15(_15_out), .in16(_16_out), .in17(_17_out), .in18(_18_out), .in19(_19_out),
    .in20(_20_out), .in21(_21_out), .in22(_22_out), .in23(_23_out), .in24(_24_out), .in25(_25_out),
    .in26(_26_out), .in27(_27_out), .in28(_28_out), .in29(_29_out), .in30(_30_out), .in31(_31_out),
    .out(RD2), .sel(A2));  // open: en
  Register #(.width(32)) register_9 (.D(_2_in), .en(WE), .Q(_2_out), .clk(clk), .clr(reset));
  Register #(.width(32)) register_10 (.D(_10_in), .en(WE), .Q(_10_out), .clk(clk), .clr(reset));
  Register #(.width(32)) register_11 (.D(_18_in), .en(WE), .Q(_18_out), .clk(clk), .clr(reset));
  Register #(.width(32)) register_12 (.D(_26_in), .en(WE), .Q(_26_out), .clk(clk), .clr(reset));
  Register #(.width(32)) register_13 (.D(_3_in), .en(WE), .Q(_3_out), .clk(clk), .clr(reset));
  Register #(.width(32)) register_14 (.D(_11_in), .en(WE), .Q(_11_out), .clk(clk), .clr(reset));
  Register #(.width(32)) register_15 (.D(_19_in), .en(WE), .Q(_19_out), .clk(clk), .clr(reset));
  Register #(.width(32)) register_16 (.D(_27_in), .en(WE), .Q(_27_out), .clk(clk), .clr(reset));
  Demultiplexer #(.select(5), .width(32), .tristate("true")) demultiplexer_1 (
    .out1(_1_in), .out2(_2_in), .out3(_3_in), .out4(_4_in), .out5(_5_in), .out6(_6_in), .out7(_7_in),
    .out8(_8_in), .out9(_9_in), .out10(_10_in), .out11(_11_in), .out12(_12_in), .out13(_13_in),
    .out14(_14_in), .out15(_15_in), .out16(_16_in), .out17(_17_in), .out18(_18_in), .out19(_19_in),
    .out20(_20_in), .out21(_21_in), .out22(_22_in), .out23(_23_in), .out24(_24_in), .out25(_25_in),
    .out26(_26_in), .out27(_27_in), .out28(_28_in), .out29(_29_in), .out30(_30_in), .out31(_31_in), .in(WD),
    .sel(A3));  // open: out0, en
  Register #(.width(32)) register_17 (.D(_4_in), .en(WE), .Q(_4_out), .clk(clk), .clr(reset));
  Register #(.width(32)) register_18 (.D(_12_in), .en(WE), .Q(_12_out), .clk(clk), .clr(reset));
  Register #(.width(32)) register_19 (.D(_20_in), .en(WE), .Q(_20_out), .clk(clk), .clr(reset));
  Register #(.width(32)) register_20 (.D(_28_in), .en(WE), .Q(_28_out), .clk(clk), .clr(reset));
  Register #(.width(32)) register_21 (.D(_5_in), .en(WE), .Q(_5_out), .clk(clk), .clr(reset));
  Register #(.width(32)) register_22 (.D(_13_in), .en(WE), .Q(_13_out), .clk(clk), .clr(reset));
  Register #(.width(32)) register_23 (.D(_21_in), .en(WE), .Q(_21_out), .clk(clk), .clr(reset));
  Register #(.width(32)) register_24 (.D(_29_in), .en(WE), .Q(_29_out), .clk(clk), .clr(reset));
  Register #(.width(32)) register_25 (.D(_6_in), .en(WE), .Q(_6_out), .clk(clk), .clr(reset));
  Register #(.width(32)) register_26 (.D(_14_in), .en(WE), .Q(_14_out), .clk(clk), .clr(reset));
  Register #(.width(32)) register_27 (.D(_22_in), .en(WE), .Q(_22_out), .clk(clk), .clr(reset));
  Register #(.width(32)) register_28 (.D(_30_in), .en(WE), .Q(_30_out), .clk(clk), .clr(reset));
  Register #(.width(32)) register_29 (.D(_7_in), .en(WE), .Q(_7_out), .clk(clk), .clr(reset));
  Register #(.width(32)) register_30 (.D(_15_in), .en(WE), .Q(_15_out), .clk(clk), .clr(reset));
  Register #(.width(32)) register_31 (.D(_23_in), .en(WE), .Q(_23_out), .clk(clk), .clr(reset));
  Register #(.width(32)) register_32 (.D(_31_in), .en(WE), .Q(_31_out), .clk(clk), .clr(reset));
endmodule

module test (
  input  in_1,
  input  in_2,
  input  in_3,
  input  in_4,
  input  in_5,
  input  in_6,
  input  in_7
);

  DM dm_1 (.in_1(32'h4), .WD(32'h9), .WE(in_2), .clk(in_1), .rst(in_4), .mode(in_3));  // open: RD
  RAM #(.addrWidth(12), .dataWidth(32), .bus("separate")) ram_1 (
    .addr(12'h1), .din(32'h9), .str(in_5), .clk(in_6), .clr(in_7));  // open: data, sel, ld
endmodule

module IFU (
  input  [31:0] in_1,
  output [31:0] out_2
);

  wire [11:0] instrPos;
  wire [31:0] subtractor_1_out;
  wire [31:12] shifter_1_out;

  Subtractor #(.width(32)) subtractor_1 (.a(in_1), .b(32'h3000), .out(subtractor_1_out));  // open: bin, bout
  ROM #(.addrWidth(12), .dataWidth(32)) rom_1 (.addr(instrPos), .data(out_2));  // open: sel
  Shifter #(.width(32), .shift("lr")) shifter_1 (
    .in(subtractor_1_out), .\dist (5'b00010), .out({shifter_1_out, instrPos}));

  // Notes on the sheet:
  //   contents of rom_1 (hex, n*v repeats v):
  //   341c0000 341d0000 34013456 210820 8c010004 ac010004 3c027878 411822 3c051234 34040005 0 ac85ffff
  //   8c83ffff 10650001 1000000d 34670404 10e3000b 0 3c087777 3508ffff 80022 34001100 e65020 34080000
  //   34090001 340a0001 10a4020 1109fffe 1000ffff
endmodule

module ALU (
  input  [31:0] num1,
  input  [2:0] ALUop,
  input  [31:0] num2,
  input  [4:0] S,
  output [31:0] out_5,
  output out_6
);

  wire [31:0] add, \and , div, lui, mul, \or , sll, sra, srl, sub;

  Comparator #(.width(32)) comparator_1 (.a(num1), .b(num2), .eq(out_6));  // open: gt, lt
  Adder #(.width(32)) adder_1 (.a(num1), .b(num2), .out(add));  // open: cin, cout
  Subtractor #(.width(32)) subtractor_1 (.a(num1), .b(num2), .out(sub));  // open: bin, bout
  Multiplier #(.width(32)) multiplier_1 (.a(num1), .b(num2), .out(mul));  // open: cin, cout
  Divider #(.width(32)) divider_1 (.a(num1), .b(num2), .out(div));  // open: upper, rem
  assign \or  = num1 | num2;  // OR_Gate or_1, 32 bits wide
  assign \and  = num1 & num2;  // AND_Gate and_1, 32 bits wide
  Shifter #(.width(32)) shifter_1 (.in(num1), .\dist (S), .out(sll));
  Shifter #(.width(32), .shift("lr")) shifter_2 (.in(num1), .\dist (S), .out(srl));
  Shifter #(.width(32), .shift("ar")) shifter_3 (.in(num1), .\dist (S), .out(sra));
  Shifter #(.width(32)) shifter_4 (.in(num2), .\dist (5'b10000), .out(lui));
  Multiplexer #(.select(3), .width(32)) multiplexer_1 (
    .in0({32{1'b0}}), .in1(add), .in2(sub), .in3(\or ), .in4(lui), .out(out_5), .sel(ALUop));  // open: in5, in6, in7, en
endmodule

module EXT (
  input  [15:0] imm16,
  input  in_2,
  output [31:0] out_3
);

  wire [31:0] bit_extender_1_out, bit_extender_2_out;

  assign bit_extender_1_out = {{16{1'b0}}, imm16};  // Bit_Extender bit_extender_1
  assign bit_extender_2_out = {{16{imm16[15]}}, imm16};  // Bit_Extender bit_extender_2
  Multiplexer #(.width(32)) multiplexer_1 (
    .in0(bit_extender_1_out), .in1(bit_extender_2_out), .out(out_3), .sel(in_2));  // open: en
endmodule

module NPC (
  input  [31:0] PC,
  input  bge,
  input  [15:0] imm16,
  input  Zero,
  output [31:0] NPC
);

  wire and_1_out;
  wire [29:0] bit_extender_1_out;
  wire [31:0] adder_1_out, adder_2_out;

  Adder #(.width(32)) adder_1 (.a(PC), .b(32'h4), .out(adder_1_out));  // open: cin, cout
  assign bit_extender_1_out = {{14{imm16[15]}}, imm16};  // Bit_Extender bit_extender_1
  Adder #(.width(32)) adder_2 (.a(adder_1_out), .b({bit_extender_1_out, 2'b00}), .out(adder_2_out));  // open: cin, cout
  Multiplexer #(.width(32)) multiplexer_1 (
    .in0(adder_1_out), .in1(adder_2_out), .out(NPC), .sel(and_1_out));  // open: en
  and and_1 (and_1_out, Zero, bge);
endmodule

module PC (
  input  [31:0] in_1,
  input  clk,
  input  rst,
  output [31:0] out_4
);

  wire [31:0] register_1_q, xor_1_out;

  assign xor_1_out = 32'h3000 ^ in_1;  // XOR_Gate xor_1, 32 bits wide
  Register #(.width(32)) register_1 (.D(xor_1_out), .Q(register_1_q), .clk(clk), .clr(rst));  // open: en
  assign out_4 = 32'h3000 ^ register_1_q;  // XOR_Gate xor_2, 32 bits wide
endmodule

module DM (
  input  [31:0] in_1,
  input  WE,
  input  clk,
  input  rst,
  input  [31:0] WD,
  input  mode,
  output [31:0] RD
);

  wire [7:0] multiplexer_1_out;
  wire [31:0] bit_extender_1_out, ram_1_data;

  // Probe on in_1[13:2]
  RAM #(.addrWidth(12), .dataWidth(32), .bus("separate")) ram_1 (
    .addr(in_1[13:2]), .din(WD), .data(ram_1_data), .str(WE), .clk(clk), .clr(rst));  // open: sel, ld
  Multiplexer #(.select(2), .width(8)) multiplexer_1 (
    .in0(ram_1_data[7:0]), .in1(ram_1_data[15:8]), .in2(ram_1_data[23:16]), .in3(ram_1_data[31:24]),
    .out(multiplexer_1_out), .sel(in_1[1:0]));  // open: en
  assign bit_extender_1_out = {{24{multiplexer_1_out[7]}}, multiplexer_1_out};  // Bit_Extender bit_extender_1
  Multiplexer #(.width(32)) multiplexer_2 (.in0(ram_1_data), .out(RD), .sel(mode));  // open: in1, en

  // Other names for the same wires on the sheet: byte[1:0] = in_1[1:0]

  // Notes on the sheet:
  //   little-endian   MSB in high address
  //   example:   0x 12 34 56 78     
  //   Addr:         3  2   1   0
endmodule

module Controller (
  input  [5:0] opCode,
  input  [5:0] funct,
  output RegDst,
  output SignExt,
  output ALUsrc,
  output RegWrite,
  output branch,
  output MemtoReg,
  output MemWrite,
  output [2:0] ALUop
);

  wire add, ALUadd, ALUlui, ALUor, ALUsub, beq, comparator_1_eq, comparator_2_eq, comparator_3_eq,
       comparator_4_eq, lw, ori, sub, sw;
  wire [2:0] multiplexer_1_out, multiplexer_2_out, multiplexer_3_out;

  buf or_1 (MemtoReg, lw);  // OR_Gate
  buf or_2 (MemWrite, sw);  // OR_Gate
  Comparator #(.width(6)) comparator_1 (.a(opCode), .b({6{1'b0}}), .eq(comparator_1_eq));  // open: gt, lt
  Comparator #(.width(6)) comparator_2 (.a(funct), .b(6'b100000), .eq(comparator_2_eq));  // open: gt, lt
  Comparator #(.width(6)) comparator_3 (.a(opCode), .b({6{1'b0}}), .eq(comparator_3_eq));  // open: gt, lt
  Comparator #(.width(6)) comparator_4 (.a(funct), .b(6'b100010), .eq(comparator_4_eq));  // open: gt, lt
  Comparator #(.width(6)) comparator_5 (.a(opCode), .b(6'b001101), .eq(ori));  // open: gt, lt
  Comparator #(.width(6)) comparator_6 (.a(opCode), .b(6'b100011), .eq(lw));  // open: gt, lt
  Comparator #(.width(6)) comparator_7 (.a(opCode), .b(6'b101011), .eq(sw));  // open: gt, lt
  Comparator #(.width(6)) comparator_8 (.a(opCode), .b(6'b000100), .eq(beq));  // open: gt, lt
  Comparator #(.width(6)) comparator_9 (.a(opCode), .b(6'b001111), .eq(ALUlui));  // open: gt, lt
  and and_1 (add, comparator_1_eq, comparator_2_eq);
  and and_2 (sub, comparator_3_eq, comparator_4_eq);
  Multiplexer #(.width(3)) multiplexer_1 (
    .in0(3'b000), .in1(3'b001), .out(multiplexer_1_out), .sel(ALUadd));  // open: en
  or or_3 (RegDst, add, sub);
  Multiplexer #(.width(3)) multiplexer_2 (
    .in0(multiplexer_1_out), .in1(3'b010), .out(multiplexer_2_out), .sel(ALUsub));  // open: en
  Multiplexer #(.width(3)) multiplexer_3 (
    .in0(multiplexer_2_out), .in1(3'b011), .out(multiplexer_3_out), .sel(ALUor));  // open: en
  or or_4 (SignExt, lw, sw);
  Multiplexer #(.width(3)) multiplexer_4 (
    .in0(multiplexer_3_out), .in1(3'b100), .out(ALUop), .sel(ALUlui));  // open: en
  or or_5 (ALUsrc, lw, sw, ori, ALUlui);
  or or_6 (RegWrite, add, sub, lw, ori, ALUlui);
  buf or_7 (branch, beq);  // OR_Gate
  or or_8 (ALUadd, add, lw, sw);
  buf or_9 (ALUsub, sub);  // OR_Gate
  buf or_10 (ALUor, ori);  // OR_Gate

  // Other names for the same wires on the sheet: lui = ALUlui

  // Notes on the sheet:
  //   RegDst=1, write to rd
  //   ALUsrc=1, imm as srcB
endmodule

module main (
  input  in_1,
  output [31:0] Instr,
  output [31:0] PC,
  output RegWrite,
  output [4:0] RegAddr,
  output [31:0] RegData,
  output MemWrite,
  output [31:0] MemAddr,
  output [31:0] MemData
);

  wire ALUsrc, branch, clk, equal, MemtoReg, RegDst, SignExt;
  wire [2:0] ALUop;
  wire [31:0] ext_1_out_3, loadMem, multiplexer_3_out, npc_1_npc, reg1Value;

  // Probe on Instr[25:21]
  NPC npc_1 (.PC(PC), .imm16(Instr[15:0]), .Zero(equal), .NPC(npc_1_npc), .bge(branch));
  grf grf_1 (
    .clk(clk), .WE(RegWrite), .reset(in_1), .WD(RegData), .A1(Instr[25:21]), .A2(Instr[20:16]), .A3(RegAddr),
    .RD1(reg1Value), .RD2(MemData));
  Multiplexer #(.width(32)) multiplexer_1 (.in0(MemAddr), .in1(loadMem), .out(RegData), .sel(MemtoReg));  // open: en
  PC pc_1 (.in_1(npc_1_npc), .out_4(PC), .clk(clk), .rst(in_1));
  IFU ifu_1 (.in_1(PC), .out_2(Instr));
  Multiplexer #(.width(5)) multiplexer_2 (
    .in0(Instr[20:16]), .in1(Instr[15:11]), .out(RegAddr), .sel(RegDst));  // open: en
  EXT ext_1 (.imm16(Instr[15:0]), .out_3(ext_1_out_3), .in_2(SignExt));
  Clock clock_1 (.out(clk));
  Multiplexer #(.width(32)) multiplexer_3 (
    .in0(MemData), .in1(ext_1_out_3), .out(multiplexer_3_out), .sel(ALUsrc));  // open: en
  Controller controller_1 (
    .opCode(Instr[31:26]), .funct(Instr[5:0]), .RegDst(RegDst), .SignExt(SignExt), .ALUsrc(ALUsrc),
    .RegWrite(RegWrite), .branch(branch), .MemtoReg(MemtoReg), .MemWrite(MemWrite), .ALUop(ALUop));
  ALU alu_1 (
    .num1(reg1Value), .num2(multiplexer_3_out), .S(Instr[10:6]), .out_5(MemAddr), .out_6(equal), .ALUop(ALUop));
  // Probe on Instr[15:11]
  // Probe on Instr[20:16]
  DM dm_1 (.in_1(MemAddr), .WD(MemData), .RD(loadMem), .WE(MemWrite), .clk(clk), .rst(in_1), .mode(1'b0));

  // Other names for the same wires on the sheet: funct[5:0] = Instr[5:0]; imm16[15:0] = Instr[15:0];
  //   imm26[25:0] = Instr[25:0]; shamt[4:0] = Instr[10:6]; rd[4:0] = Instr[15:11]; rt[4:0] = Instr[20:16];
  //   rs[4:0] = Instr[25:21]; OpCode[5:0] = Instr[31:26]; Reg2Value[31:0] = MemData; res[31:0] = MemAddr;
  //   reset = in_1

  // Notes on the sheet:
  //   add sub ori lw sw beq lui nop
endmodule
